// Logisim project WARMUP.circ as structural Verilog
module WARMUP (
  input  A,
  input  B,
  output F
);

  wire not_1_out;

  not not_1 (not_1_out, B);
  and and_1 (F, A, not_1_out);
endmodule
